# Fritzing sketch electronics (saved by Fritzing 0.9.2b)
breadboards: 3

parts:
  Part1 = Arduino Mega 2560 (Rev3)
  LED1 = RGB LED (com. cathode, rgb) [package="5 mm [THT]"]
  R1 = Resistor [tolerance=±5% resistance=220 package=THT]
  R2 = Resistor [tolerance=±5% resistance=100 package=THT]
  R3 = Resistor [tolerance=±5% resistance=100 package=THT]
  LED2 = RGB LED (com. cathode, rgb) [package="5 mm [THT]"]
  LED3 = RGB LED (com. cathode, rgb) [package="5 mm [THT]"]
  R4 = Resistor [tolerance=±5% resistance=220 package=THT]
  R5 = Resistor [tolerance=±5% resistance=100 package=THT]
  R6 = Resistor [tolerance=±5% resistance=100 package=THT]
  R7 = Resistor [tolerance=±5% resistance=220 package=THT]
  R8 = Resistor [tolerance=±5% resistance=100 package=THT]
  R9 = Resistor [tolerance=±5% resistance=100 package=THT]
  LED4 = RGB LED (com. cathode, rgb) [package="5 mm [THT]"]
  LED5 = RGB LED (com. cathode, rgb) [package="5 mm [THT]"]
  R10 = Resistor [tolerance=±5% resistance=220 package=THT]
  R11 = Resistor [tolerance=±5% resistance=220 package=THT]
  R12 = Resistor [tolerance=±5% resistance=100 package=THT]
  R13 = Resistor [tolerance=±5% resistance=100 package=THT]
  R14 = Resistor [tolerance=±5% resistance=100 package=THT]
  R15 = Resistor [tolerance=±5% resistance=100 package=THT]
  LED6 = RGB LED (com. cathode, rgb) [package="5 mm [THT]"]
  LED7 = RGB LED (com. cathode, rgb) [package="5 mm [THT]"]
  LED8 = RGB LED (com. cathode, rgb) [package="5 mm [THT]"]
  LED9 = RGB LED (com. cathode, rgb) [package="5 mm [THT]"]
  LED10 = RGB LED (com. cathode, rgb) [package="5 mm [THT]"]
  R16 = Resistor [tolerance=±5% resistance=220 package=THT]
  R17 = Resistor [tolerance=±5% resistance=100 package=THT]
  R18 = Resistor [tolerance=±5% resistance=100 package=THT]
  R19 = Resistor [tolerance=±5% resistance=220 package=THT]
  R20 = Resistor [tolerance=±5% resistance=100 package=THT]
  R21 = Resistor [tolerance=±5% resistance=100 package=THT]
  R22 = Resistor [tolerance=±5% resistance=220 package=THT]
  R23 = Resistor [tolerance=±5% resistance=100 package=THT]
  R24 = Resistor [tolerance=±5% resistance=100 package=THT]
  R25 = Resistor [tolerance=±5% resistance=220 package=THT]
  R26 = Resistor [tolerance=±5% resistance=100 package=THT]
  R27 = Resistor [tolerance=±5% resistance=100 package=THT]
  R28 = Resistor [tolerance=±5% resistance=220 package=THT]
  R29 = Resistor [tolerance=±5% resistance=100 package=THT]
  R30 = Resistor [tolerance=±5% resistance=100 package=THT]
  S1 = Pushbutton [package="[THT]"]
  S2 = Pushbutton [package="[THT]"]
  S3 = Pushbutton [package="[THT]"]
  S4 = Pushbutton [package="[THT]"]
  S5 = Pushbutton [package="[THT]"]
  S6 = Pushbutton [package="[THT]"]
  S7 = Pushbutton [package="[THT]"]
  S8 = Pushbutton [package="[THT]"]
  S9 = Pushbutton [package="[THT]"]
  S10 = Pushbutton [package="[THT]"]
  S11 = Pushbutton [package="[THT]"]
  S12 = Pushbutton [package="[THT]"]
  S13 = Pushbutton [package="[THT]"]
  S14 = Pushbutton [package="[THT]"]
  S15 = Pushbutton [package="[THT]"]
  U3 = mystery part, 3 pins [chip_label=?]
  X1 = USB Connectors [package=usb-b-pth]
  U4 = LIPO-1000mAh [package=lipo-1000]

nets:
  N1: Part1.GND, LED1.common_cathode, LED2.common_cathode, LED3.common_cathode, LED4.common_cathode, LED5.common_cathode, LED6.common_cathode, LED7.common_cathode, LED8.common_cathode, LED9.common_cathode, LED10.common_cathode, S1.Pin_1, S1.Pin_2, S2.Pin_1, S2.Pin_2, S3.Pin_1, S3.Pin_2, S4.Pin_1, S4.Pin_2, S5.Pin_1, S5.Pin_2, S6.Pin_1, S6.Pin_2, S7.Pin_1, S7.Pin_2, S8.Pin_1, S8.Pin_2, S9.Pin_1, S9.Pin_2, S10.Pin_1, S10.Pin_2, S11.Pin_1, S11.Pin_2, S12.Pin_1, S12.Pin_2, S14.Pin_1, S14.Pin_2, S15.Pin_1, S15.Pin_2
  N2: Part1.D13_PWM, R26.Pin_1, R29.Pin_1
  N3: Part1.D12_PWM, R27.Pin_1, R30.Pin_1
  N4: Part1.D11_PWM, R25.Pin_1, R28.Pin_1
  N5: Part1.D10_PWM, R17.Pin_1, R20.Pin_1, R24.Pin_1
  N6: Part1.D9_PWM, R18.Pin_1, R21.Pin_1, R23.Pin_1
  N7: Part1.D8_PWM, R16.Pin_1, R19.Pin_1, R22.Pin_1
  N8: Part1.D2_PWM, R1.Pin_1, R4.Pin_1, R7.Pin_1
  N9: Part1.D3_PWM, R2.Pin_1, R6.Pin_1, R8.Pin_1
  N10: Part1.D4_PWM, R3.Pin_1, R5.Pin_1, R9.Pin_1
  N11: Part1.D5_PWM, R10.Pin_1, R11.Pin_1
  N12: Part1.D6_PWM, R13.Pin_1, R14.Pin_1
  N13: Part1.D7_PWM, R12.Pin_1, R15.Pin_1
  N14: Part1.D40, S14.Pin_3, S14.Pin_4
  N15: Part1.D41, S15.Pin_3, S15.Pin_4
  N16: Part1.D42, S11.Pin_3, S11.Pin_4
  N17: Part1.D43, S12.Pin_3, S12.Pin_4
  N18: Part1.D44, S9.Pin_3, S9.Pin_4
  N19: Part1.D45, S10.Pin_3, S10.Pin_4
  N20: Part1.D46, S7.Pin_3, S7.Pin_4
  N21: Part1.D47, S8.Pin_3, S8.Pin_4
  N22: Part1.D48, S5.Pin_3, S5.Pin_4
  N23: Part1.D49, S6.Pin_3, S6.Pin_4
  N24: Part1.D50, S3.Pin_3, S3.Pin_4
  N25: Part1.D51, S4.Pin_3, S4.Pin_4
  N26: Part1.D52, S1.Pin_3, S1.Pin_4
  N27: Part1.D53, S2.Pin_3, S2.Pin_4
  N28: LED1.red_anode, R1.Pin_0
  N29: LED1.green_anode, R2.Pin_0
  N30: LED1.blue_anode, R3.Pin_0
  N31: LED2.red_anode, R4.Pin_0
  N32: LED2.green_anode, R6.Pin_0
  N33: LED2.blue_anode, R5.Pin_0
  N34: LED3.red_anode, R11.Pin_0
  N35: LED3.green_anode, R14.Pin_0
  N36: LED3.blue_anode, R15.Pin_0
  N37: R7.Pin_0, LED4.red_anode
  N38: R8.Pin_0, LED4.green_anode
  N39: R9.Pin_0, LED4.blue_anode
  N40: LED5.red_anode, R10.Pin_0
  N41: LED5.green_anode, R13.Pin_0
  N42: LED5.blue_anode, R12.Pin_0
  N43: LED6.red_anode, R16.Pin_0
  N44: LED6.green_anode, R18.Pin_0
  N45: LED6.blue_anode, R17.Pin_0
  N46: LED7.red_anode, R25.Pin_0
  N47: LED7.green_anode, R27.Pin_0
  N48: LED7.blue_anode, R26.Pin_0
  N49: LED8.red_anode, R28.Pin_0
  N50: LED8.green_anode, R30.Pin_0
  N51: LED8.blue_anode, R29.Pin_0
  N52: LED9.red_anode, R22.Pin_0
  N53: LED9.green_anode, R23.Pin_0
  N54: LED9.blue_anode, R24.Pin_0
  N55: LED10.red_anode, R19.Pin_0
  N56: LED10.green_anode, R21.Pin_0
  N57: LED10.blue_anode, R20.Pin_0
  N58: S13.Pin_1, S13.Pin_2, U3.pin1
  N59: S13.Pin_3, S13.Pin_4, U3.pin2, U4.-
  N60: U3.pin3, X1.VBUS, U4.+
